// Logisim project Questao-7.circ as structural Verilog: 1 circuit, main circuit main
module main (
  input  CLK,
  output S2,
  output S1,
  output S0
);

  wire and_1_out, and_2_out, and_3_out, and_4_out, and_5_out, and_6_out, and_8_out, and_9_out, and_10_out,
       d_ff_1_q, d_ff_2_q, d_ff_3_q, not_1_out, not_2_out, not_3_out, not_4_out, not_5_out, not_6_out,
       not_7_out, not_8_out, not_9_out, not_10_out, not_11_out, or_1_out, or_2_out, or_3_out;

  not not_1 (not_1_out, d_ff_2_q);
  not not_2 (not_2_out, d_ff_2_q);
  not not_3 (not_3_out, d_ff_1_q);
  not not_4 (not_4_out, d_ff_3_q);
  not not_5 (not_5_out, d_ff_1_q);
  not not_6 (not_6_out, d_ff_3_q);
  not not_7 (not_7_out, d_ff_2_q);
  not not_8 (not_8_out, d_ff_3_q);
  and and_1 (and_1_out, d_ff_1_q, not_1_out);
  or or_1 (or_1_out, and_1_out, and_2_out);
  and and_2 (and_2_out, d_ff_2_q, d_ff_3_q);
  and and_3 (and_3_out, not_2_out, d_ff_3_q);
  or or_2 (or_2_out, and_3_out, and_4_out);
  and and_4 (and_4_out, not_3_out, d_ff_2_q, not_4_out);
  and and_5 (and_5_out, not_5_out, not_6_out);
  or or_3 (or_3_out, and_5_out, and_6_out);
  and and_6 (and_6_out, not_7_out, not_8_out);
  D_Flip_Flop d_ff_1 (.clk(CLK), .D(or_1_out), .Q(d_ff_1_q));  // open: Qn, preset, en, reset
  D_Flip_Flop d_ff_2 (.clk(CLK), .D(or_2_out), .Q(d_ff_2_q));  // open: Qn, preset, en, reset
  D_Flip_Flop d_ff_3 (.clk(CLK), .D(or_3_out), .Q(d_ff_3_q));  // open: Qn, preset, en, reset
  not not_9 (not_9_out, d_ff_3_q);
  not not_10 (not_10_out, d_ff_2_q);
  and and_7 (S2, d_ff_2_q, not_11_out);
  not not_11 (not_11_out, d_ff_3_q);
  or or_4 (S1, d_ff_1_q, and_8_out);
  and and_8 (and_8_out, d_ff_2_q, d_ff_3_q);
  and and_9 (and_9_out, d_ff_2_q, not_9_out);
  or or_5 (S0, and_9_out, and_10_out);
  and and_10 (and_10_out, not_10_out, d_ff_3_q);
endmodule
