// Logisim project Trabalho-arq-extra.circ as structural Verilog: 6 circuits, main circuit 0a9
module _0a9 (
  input  CLK,
  input  CLR,
  output [3:0] SAIDA,
  output out_4
);

  wire and_1_out, and_2_out, not_1_out, not_2_out, or_1_out;

  T_Flip_Flop t_ff_1 (.clk(CLK), .T(1'b1), .Q(SAIDA[0]), .reset(or_1_out));  // open: Qn, preset, en
  T_Flip_Flop t_ff_2 (.clk(CLK), .T(SAIDA[0]), .Q(SAIDA[1]), .reset(or_1_out));  // open: Qn, preset, en
  and and_1 (and_1_out, SAIDA[1], SAIDA[0]);
  T_Flip_Flop t_ff_3 (.clk(CLK), .T(and_1_out), .Q(SAIDA[2]), .reset(or_1_out));  // open: Qn, preset, en
  and and_2 (and_2_out, and_1_out, SAIDA[2]);
  T_Flip_Flop t_ff_4 (.clk(CLK), .T(and_2_out), .Q(SAIDA[3]), .reset(or_1_out));  // open: Qn, preset, en
  or or_1 (or_1_out, out_4, CLR);
  not not_1 (not_1_out, SAIDA[0]);
  not not_2 (not_2_out, SAIDA[2]);
  and and_3 (out_4, not_1_out, SAIDA[1], not_2_out, SAIDA[3]);
endmodule

module Oa59 (
  input  CLK,
  output [3:0] S1,
  output [3:0] S0,
  output PROX_CLK
);

  wire n0a9_2_out_4, not_1_out, not_2_out;

  not not_1 (not_1_out, S1[3]);
  not not_2 (not_2_out, S1[0]);
  and and_1 (PROX_CLK, not_1_out, S1[2], S1[1], not_2_out);
  _0a9 u_0a9_1 (.CLK(n0a9_2_out_4), .CLR(PROX_CLK), .SAIDA(S1));  // open: out_4
  _0a9 u_0a9_2 (.CLK(CLK), .SAIDA(S0), .out_4(n0a9_2_out_4));  // open: CLR
endmodule

module oa23 (
  input  CLK,
  output [3:0] S0,
  output [3:0] S1
);

  wire and_1_out, and_2_out, and_3_out, n0a9_2_out_4, not_1_out, not_2_out, not_3_out, not_4_out, not_5_out,
       not_6_out;

  Projeto_12 projeto_12_1 ();
  not not_1 (not_1_out, S1[2]);
  not not_2 (not_2_out, S1[3]);
  and and_1 (and_1_out, not_2_out, not_1_out, S1[1], not_3_out);
  _0a9 u_0a9_1 (.CLK(n0a9_2_out_4), .CLR(and_3_out), .SAIDA(S1));  // open: out_4
  not not_3 (not_3_out, S1[0]);
  not not_4 (not_4_out, S0[0]);
  not not_5 (not_5_out, S0[1]);
  not not_6 (not_6_out, S0[3]);
  and and_2 (and_2_out, not_6_out, S0[2], not_5_out, not_4_out);
  and and_3 (and_3_out, and_1_out, and_2_out);
  _0a9 u_0a9_2 (.CLK(CLK), .CLR(and_3_out), .SAIDA(S0), .out_4(n0a9_2_out_4));
endmodule

module _0a11 (
  input  CLK,
  output [3:0] S0,
  output [3:0] S1,
  output SAIDA_AM_PM
);

  wire and_1_out, and_2_out, and_3_out, n0a9_2_out_4, not_1_out, not_2_out, not_3_out, not_4_out, not_5_out,
       not_6_out;

  not not_1 (not_1_out, S1[2]);
  not not_2 (not_2_out, S1[3]);
  and and_1 (and_1_out, not_2_out, not_1_out, not_3_out, S1[0]);
  T_Flip_Flop t_ff_1 (.clk(and_3_out), .T(1'b1), .Q(SAIDA_AM_PM));  // open: Qn, preset, reset, en
  _0a9 u_0a9_1 (.CLK(n0a9_2_out_4), .CLR(and_3_out), .SAIDA(S1));  // open: out_4
  not not_3 (not_3_out, S1[1]);
  not not_4 (not_4_out, S0[3]);
  not not_5 (not_5_out, S0[0]);
  not not_6 (not_6_out, S0[2]);
  and and_2 (and_2_out, not_4_out, not_6_out, S0[1], not_5_out);
  and and_3 (and_3_out, and_1_out, and_2_out);
  _0a9 u_0a9_2 (.CLK(CLK), .CLR(and_3_out), .SAIDA(S0), .out_4(n0a9_2_out_4));
endmodule

module Projeto_12 (
);

  wire clock_1_out, n0a11_1_saida_am_pm, not_1_out, oa59_1_prox_clk;
  wire [3:0] n0a11_1_s0, n0a11_1_s1, oa59_1_s0, oa59_1_s1;

  not not_1 (not_1_out, n0a11_1_saida_am_pm);
  LED AM (.in(not_1_out));
  LED PM (.in(n0a11_1_saida_am_pm));
  _0a11 u_0a11_1 (.S0(n0a11_1_s0), .S1(n0a11_1_s1), .CLK(oa59_1_prox_clk), .SAIDA_AM_PM(n0a11_1_saida_am_pm));
  Hex_Digit_Display hex_digit_display_1 (.value(n0a11_1_s1));  // open: dp
  Hex_Digit_Display hex_digit_display_2 (.value(n0a11_1_s0));  // open: dp
  Hex_Digit_Display hex_digit_display_3 (.value(oa59_1_s1));  // open: dp
  Oa59 oa59_1 (.CLK(clock_1_out), .S1(oa59_1_s1), .S0(oa59_1_s0), .PROX_CLK(oa59_1_prox_clk));
  Hex_Digit_Display hex_digit_display_4 (.value(oa59_1_s0));  // open: dp
  Clock clock_1 (.out(clock_1_out));
endmodule

module Projeto_24 (
);

  wire clock_1_out, oa59_1_prox_clk;
  wire [3:0] oa23_1_s0, oa23_1_s1, oa59_1_s0, oa59_1_s1;

  Hex_Digit_Display hex_digit_display_1 (.value(oa23_1_s1));  // open: dp
  oa23 oa23_1 (.S0(oa23_1_s0), .S1(oa23_1_s1), .CLK(oa59_1_prox_clk));
  Hex_Digit_Display hex_digit_display_2 (.value(oa23_1_s0));  // open: dp
  Hex_Digit_Display hex_digit_display_3 (.value(oa59_1_s1));  // open: dp
  Oa59 oa59_1 (.CLK(clock_1_out), .S1(oa59_1_s1), .S0(oa59_1_s0), .PROX_CLK(oa59_1_prox_clk));
  Hex_Digit_Display hex_digit_display_4 (.value(oa59_1_s0));  // open: dp
  Clock clock_1 (.out(clock_1_out));
endmodule
