// Logisim project Questao-6.circ as structural Verilog: 1 circuit, main circuit main
module main (
  input  d,
  output S3,
  output S2,
  output S1,
  output S0
);

  wire and_1_out, and_2_out, and_3_out, and_4_out, CLK_out, d_ff_1_q, d_ff_2_q, not_1_out, not_2_out,
       not_3_out, not_4_out, not_5_out, not_6_out, not_7_out, not_8_out, not_9_out, or_1_out;

  Clock CLK (.out(CLK_out));
  not not_1 (not_1_out, d);
  not not_2 (not_2_out, d_ff_1_q);
  not not_3 (not_3_out, d_ff_2_q);
  not not_4 (not_4_out, d);
  not not_5 (not_5_out, d_ff_2_q);
  not not_6 (not_6_out, d_ff_1_q);
  and and_1 (and_1_out, not_1_out, not_2_out, not_3_out);
  and and_2 (and_2_out, not_4_out, d_ff_1_q, d_ff_2_q);
  and and_3 (and_3_out, d, d_ff_1_q, not_5_out);
  and and_4 (and_4_out, d, not_6_out, d_ff_2_q);
  not not_7 (not_7_out, d_ff_2_q);
  or or_1 (or_1_out, and_1_out, and_2_out, and_3_out, and_4_out);
  D_Flip_Flop d_ff_1 (.clk(CLK_out), .D(or_1_out), .Q(d_ff_1_q));  // open: Qn, preset, en, reset
  D_Flip_Flop d_ff_2 (.clk(CLK_out), .D(not_7_out), .Q(d_ff_2_q));  // open: Qn, preset, en, reset
  and and_5 (S3, d_ff_2_q, d_ff_1_q);
  and and_6 (S2, d_ff_1_q, not_8_out);
  not not_8 (not_8_out, d_ff_2_q);
  not not_9 (not_9_out, d_ff_1_q);
  and and_7 (S1, not_9_out, d_ff_2_q);

  assign S0 = 1'b0;
endmodule
