// Logisim project EP01.circ as structural Verilog: 4 circuits, main circuit Somador 1/2
module main (
  input  A0,
  input  A1,
  input  A2,
  input  A3,
  input  Ci0,
  input  B0,
  input  B1,
  input  B2,
  input  B3,
  output Overflow,
  output Co0
);

  wire displaydecoder_1_p2, displaydecoder_1_p3, displaydecoder_1_p4, displaydecoder_1_p5,
       displaydecoder_1_p6, displaydecoder_1_p7, displaydecoder_1_p8, displaydecoder_2_p2,
       displaydecoder_2_p3, displaydecoder_2_p4, displaydecoder_2_p5, displaydecoder_2_p6,
       displaydecoder_2_p7, displaydecoder_2_p8, displaydecoder_3_p2, displaydecoder_3_p3,
       displaydecoder_3_p4, displaydecoder_3_p5, displaydecoder_3_p6, displaydecoder_3_p7,
       displaydecoder_3_p8;
  wire [3:0] somador_4_1_s0;

  Somador_4 somador_4_1 (
    .A0(A0), .S0(somador_4_1_s0[0]), .A1(A1), .S1(somador_4_1_s0[1]), .A2(A2), .S2(somador_4_1_s0[2]),
    .A3(A3), .S3(somador_4_1_s0[3]), .B0(B0), .B1(B1), .B2(B2), .B3(B3), .Ci0(Ci0), .Co3(Co0),
    .Overflow(Overflow));
  // DisplayDecoder displaydecoder_1: pin names not known; wires that end beside it: {A3, A2, A1, A0}, displaydecoder_1_p2, displaydecoder_1_p3, displaydecoder_1_p4, displaydecoder_1_p5, displaydecoder_1_p6, displaydecoder_1_p7, displaydecoder_1_p8
  // DisplayDecoder displaydecoder_2: pin names not known; wires that end beside it: {B3, B2, B1, B0}, displaydecoder_2_p2, displaydecoder_2_p3, displaydecoder_2_p4, displaydecoder_2_p5, displaydecoder_2_p6, displaydecoder_2_p7, displaydecoder_2_p8
  _7_Segment_Display u_7_segment_display_1 (
    .g(displaydecoder_1_p8), .f(displaydecoder_1_p7), .a(displaydecoder_1_p2), .b(displaydecoder_1_p3),
    .e(displaydecoder_1_p6), .d(displaydecoder_1_p5), .c(displaydecoder_1_p4));  // open: dp
  // DisplayDecoder displaydecoder_3: pin names not known; wires that end beside it: somador_4_1_s0, displaydecoder_3_p2, displaydecoder_3_p3, displaydecoder_3_p4, displaydecoder_3_p5, displaydecoder_3_p6, displaydecoder_3_p7, displaydecoder_3_p8
  _7_Segment_Display u_7_segment_display_2 (
    .g(displaydecoder_2_p8), .f(displaydecoder_2_p7), .a(displaydecoder_2_p2), .b(displaydecoder_2_p3),
    .e(displaydecoder_2_p6), .d(displaydecoder_2_p5), .c(displaydecoder_2_p4));  // open: dp
  _7_Segment_Display u_7_segment_display_3 (
    .g(displaydecoder_3_p8), .f(displaydecoder_3_p7), .a(displaydecoder_3_p2), .b(displaydecoder_3_p3),
    .e(displaydecoder_3_p6), .d(displaydecoder_3_p5), .c(displaydecoder_3_p4));  // open: dp
endmodule

module Somador_1_2 (
  input  A0,
  input  B0,
  output Soma,
  output Carry_Out
);

  xor xor_1 (Soma, A0, B0);
  and and_1 (Carry_Out, A0, B0);
endmodule

module Somador_1 (
  input  A0,
  input  B0,
  input  Ci0,
  output S0,
  output Co0
);

  wire somador_1_2_1_carry_out, somador_1_2_1_soma, somador_1_2_2_carry_out;

  Somador_1_2 somador_1_2_1 (.A0(A0), .B0(B0), .Soma(somador_1_2_1_soma), .Carry_Out(somador_1_2_1_carry_out));
  Somador_1_2 somador_1_2_2 (.A0(somador_1_2_1_soma), .B0(Ci0), .Soma(S0), .Carry_Out(somador_1_2_2_carry_out));
  or or_1 (Co0, somador_1_2_2_carry_out, somador_1_2_1_carry_out);
endmodule

module Somador_4 (
  input  A0,
  input  A1,
  input  A2,
  input  A3,
  input  Ci0,
  input  B0,
  input  B1,
  input  B2,
  input  B3,
  output S0,
  output S1,
  output S2,
  output S3,
  output Co3,
  output Overflow
);

  wire somador_1_1_co0, somador_1_2_co0, somador_1_3_co0;

  Somador_1 somador_1_1 (.A0(A0), .B0(B0), .Ci0(Ci0), .S0(S0), .Co0(somador_1_1_co0));
  Somador_1 somador_1_2 (.A0(A1), .B0(B1), .Ci0(somador_1_1_co0), .S0(S1), .Co0(somador_1_2_co0));
  Somador_1 somador_1_3 (.A0(A2), .B0(B2), .Ci0(somador_1_2_co0), .S0(S2), .Co0(somador_1_3_co0));
  Somador_1 somador_1_4 (.A0(A3), .B0(B3), .Ci0(somador_1_3_co0), .S0(S3), .Co0(Co3));
  xor xor_1 (Overflow, somador_1_3_co0, Co3);
endmodule
