// Logisim project Questao-10.circ as structural Verilog: 1 circuit, main circuit main
module main (
  input  PRESET,
  input  SPRE,
  input  J,
  input  K,
  input  CLK_ENABLE,
  input  in_6,
  input  CLR,
  output Q,
  output nQ
);

  wire and_1_out, and_2_out, and_3_out, and_4_out, and_5_out, and_6_out, clock_1_out, nand_1_out, nand_2_out,
       not_1_out, not_2_out, not_3_out, not_4_out, not_5_out, not_6_out, or_1_out, or_2_out;

  Clock clock_1 (.out(clock_1_out));
  or or_1 (or_1_out, SPRE, J);
  not not_1 (not_1_out, SPRE);
  not not_2 (not_2_out, in_6);
  and and_1 (and_1_out, not_1_out, K);
  and and_2 (and_2_out, or_1_out, not_2_out);
  or or_2 (or_2_out, and_1_out, in_6);
  and and_3 (and_3_out, nQ, and_2_out);
  and and_4 (and_4_out, or_2_out, Q);
  not not_3 (not_3_out, clock_1_out);
  not not_4 (not_4_out, not_3_out);
  and and_5 (and_5_out, not_4_out, not_4_out);
  and and_6 (and_6_out, not_3_out, and_5_out);
  not not_5 (not_5_out, PRESET);
  nand nand_1 (nand_1_out, and_3_out, CLK_ENABLE, and_6_out);
  nand nand_2 (nand_2_out, and_6_out, CLK_ENABLE, and_4_out);
  not not_6 (not_6_out, CLR);
  nand nand_3 (Q, not_5_out, nand_1_out, nQ);
  nand nand_4 (nQ, Q, nand_2_out, not_6_out);

  // Notes on the sheet:
  //   CLK
  //   SCLR
endmodule
