// Logisim project Questao-5.circ as structural Verilog: 1 circuit, main circuit main
module main (
  input  PRESET,
  output SO,
  output S1,
  output S2,
  output S3
);

  wire clock_1_out;

  Clock clock_1 (.out(clock_1_out));
  D_Flip_Flop d_ff_1 (.clk(clock_1_out), .D(S3), .Q(SO), .preset(PRESET), .reset(S1));  // open: Qn, en
  D_Flip_Flop d_ff_2 (.clk(clock_1_out), .D(SO), .Q(S1), .reset(S2));  // open: Qn, preset, en
  D_Flip_Flop d_ff_3 (.clk(clock_1_out), .D(S1), .Q(S2), .reset(S3));  // open: Qn, preset, en
  D_Flip_Flop d_ff_4 (.clk(clock_1_out), .D(S2), .Q(S3), .reset(SO));  // open: Qn, preset, en

  // Notes on the sheet:
  //   CLK
endmodule
