// Logisim project EXERCICIO-11.circ as structural Verilog: 1 circuit, main circuit main
module main (
  input  B2,
  input  B1,
  input  B0,
  input  A2,
  input  A1,
  input  A0,
  output S0,
  output S1,
  output S2,
  output S3,
  output S4,
  output S5
);

  wire adder_1_cout, adder_2_cout, adder_2_out, adder_3_cout, adder_3_out, adder_5_cout, adder_6_cout,
       and_2_out, and_3_out, and_4_out, and_5_out, and_6_out, and_7_out, and_8_out, and_9_out;

  and and_1 (S0, A0, B0);
  and and_2 (and_2_out, A0, B0);
  and and_3 (and_3_out, A0, B1);
  and and_4 (and_4_out, A2, B0);
  and and_5 (and_5_out, A1, B1);
  and and_6 (and_6_out, A0, B2);
  and and_7 (and_7_out, A2, B1);
  and and_8 (and_8_out, A1, B2);
  and and_9 (and_9_out, A2, B2);
  Adder #(.width(1)) adder_1 (.a(and_2_out), .b(and_3_out), .out(S1), .cin(1'b0), .cout(adder_1_cout));
  Adder #(.width(1)) adder_2 (.a(and_4_out), .b(and_5_out), .out(adder_2_out), .cin(adder_1_cout), .cout(adder_2_cout));
  Adder #(.width(1)) adder_3 (.a(and_7_out), .b(and_8_out), .out(adder_3_out), .cin(adder_2_cout), .cout(adder_3_cout));
  Adder #(.width(1)) adder_4 (.a(adder_3_cout), .b(and_9_out), .out(S4), .cin(adder_6_cout), .cout(S5));
  Adder #(.width(1)) adder_5 (.a(adder_2_out), .b(and_6_out), .out(S2), .cin(1'b0), .cout(adder_5_cout));
  Adder #(.width(1)) adder_6 (.a(adder_3_out), .b(adder_5_cout), .out(S3), .cin(1'b0), .cout(adder_6_cout));
endmodule
